# Fritzing sketch buratino (saved by Fritzing 0.9.3b)
breadboards: 1
perfboards: 2

parts:
  R1 = Resistor [tolerance=±5% resistance=220 package=THT]  # not connected
  Q1 = NPN-Transistor [package="TO92 [THT]"]
  R2 = Resistor [tolerance=±5% resistance=220 package=THT]  # not connected
  R3 = Resistor [tolerance=±5% resistance=220 package=THT]  # not connected
  R4 = Resistor [tolerance=±5% resistance=220 package=THT]
  S1 = Pushbutton [package="[THT]"]  # not connected

nets:
  N1: Q1.C, R4.Pin_0
